# Fritzing sketch chyba_wszystko (saved by Fritzing 0.9.3b)
breadboards: 1

parts:
  7_Seg1 = 7 Segment Display
  4510 = ULN2003A [package="DIP16 [THT]"]
  4511 = ULN2003A [package="DIP16 [THT]"]
  R3 = Resistor [tolerance=±5% resistance=470 package=THT]
  R4 = Resistor [tolerance=±5% resistance=470 package=THT]
  R5 = Resistor [tolerance=±5% resistance=470 package=THT]
  R6 = Resistor [tolerance=±5% resistance=470 package=THT]
  R7 = Resistor [tolerance=±5% resistance=470 package=THT]
  R8 = Resistor [tolerance=±5% resistance=470 package=THT]
  R9 = Resistor [tolerance=±5% resistance=470 package=THT]
  Clk_G_R_U_O_V = female pin header, 6 pins [form="♀ (female)"]
  Clk_G_R_U_O_V_2 = female pin header, 6 pins [form="♀ (female)"]
  G_I_V_O = female pin header, 4 pins [form="♀ (female)"]
  G_I_V_O_2 = female pin header, 4 pins [form="♀ (female)"]
  O_V_G = female pin header, 3 pins [form="♀ (female)"]
  S_B-_B+_DB+ = female pin header, 4 pins [form="♀ (female)"]
  G_T_O_V = female pin header, 4 pins [form="♀ (female)"]
  G_T_O_V_2 = female pin header, 4 pins [form="♀ (female)"]
  Q3 = NPN-Transistor [package="TO92 [THT]"]
  Q6 = NPN-Transistor [package="TO92 [THT]"]
  O_V_G_2 = female pin header, 3 pins [form="♀ (female)"]
  R29 = Resistor [tolerance=±5% resistance=1k package=THT]
  R27 = Resistor [tolerance=±5% resistance=1k package=THT]
  R34 = Resistor [tolerance=±5% resistance=10k package=THT]
  C9 = Ceramic Capacitor [capacitance=100nF package="100 mil [THT, multilayer]"]
  R28 = Resistor [tolerance=±5% resistance=10k package=THT]
  R17 = Resistor [tolerance=±5% resistance=10k package=THT]
  LED1 = LED - 5mm [color="Red (633nm)" package="5 mm [THT]"]
  LED2 = LED - 5mm [color="Red (633nm)" package="5 mm [THT]"]
  LED4 = LED - 5mm [color="Red (633nm)" package="5 mm [THT]"]
  555 = 555 Timer [package="DIP8 [THT]"]
  R25 = Resistor [tolerance=±5% resistance=100k package=THT]
  R26 = Resistor [tolerance=±5% resistance=470 package=THT]
  C7 = Ceramic Capacitor [capacitance=100nF package="100 mil [THT, multilayer]"]
  C8 = Ceramic Capacitor [capacitance=100nF package="100 mil [THT, multilayer]"]
  Q4 = NPN-Transistor [package="TO92 [THT]"]
  Q5 = NPN-Transistor [package="TO92 [THT]"]
  R31 = Resistor [tolerance=±5% resistance=470 package=THT]
  R32 = Resistor [tolerance=±5% resistance=1k package=THT]
  J2 = Screw terminal - 2 pins [package=THT]
  J1 = Screw terminal - 2 pins [package=THT]
  R33 = Resistor [tolerance=±5% resistance=1k package=THT]
  4013 = SN74LS20N [package="DIP14 [THT]"]
  4081 = SN74LS20N [package="DIP14 [THT]"]
  4060 = ULN2003A [package="DIP16 [THT]"]
  D5 = Rectifier Diode [part_number=1N4001 package="300 mil [THT]"]
  D6Clk = Rectifier Diode [part_number=1N4001 package="300 mil [THT]"]
  D5Clk = Rectifier Diode [part_number=1N4001 package="300 mil [THT]"]
  U/D_Clk = female pin header, 2 pins [form="♀ (female)"]
  S_B-_B+_DB+_2 = female pin header, 4 pins [form="♀ (female)"]
  V = female pin header, 2 pins [form="♀ (female)"]
  G = female pin header, 2 pins [form="♀ (female)"]
  D3+ = Rectifier Diode [part_number=1N4001 package="300 mil [THT]"]
  D4- = Rectifier Diode [part_number=1N4001 package="300 mil [THT]"]
  V_O_R_G = female pin header, 4 pins [form="♀ (female)"]
  C1 = Ceramic Capacitor [capacitance=100nF package="100 mil [THT, multilayer]"]
  R1 = Resistor [tolerance=±5% resistance=220 package=THT]
  R2 = Resistor [tolerance=±5% resistance=220 package=THT]
  V_O_R_G_2 = female pin header, 4 pins [form="♀ (female)"]
  R30 = Resistor [tolerance=±5% resistance=470 package=THT]
  LED6 = LED - 5mm [color="Red (633nm)" package="5 mm [THT]"]
  Clk_R = female pin header, 2 pins [form="♀ (female)"]
  Fuse2 = Fuse with Handler [part_number=Htc-15m]
  D2 = Rectifier Diode [part_number=1N4001 package="300 mil [THT]"]
  D4 = Zener Diode [part_number=1N4732A breakdown_voltage=3.6V package="300 mil [THT]"]
  U1 = Voltage Regulator - 5V [package="TO220 [THT]"]
  + = Screw terminal - 2 pins [package=THT]
  C4 = Ceramic Capacitor [capacitance=330nF package="100 mil [THT, multilayer]"]
  C5 = Ceramic Capacitor [capacitance=100nF package="100 mil [THT, multilayer]"]
  D3 = Rectifier Diode [part_number=1N4001 package="300 mil [THT]"]
  GV = female pin header, 2 pins [form="♀ (female)"]
  GV_2 = female pin header, 2 pins [form="♀ (female)"]
  GV_3 = female pin header, 2 pins [form="♀ (female)"]
  GV2 = female pin header, 2 pins [form="♀ (female)"]
  R23 = Resistor [tolerance=±5% resistance=10k package=THT]
  R20 = Resistor [tolerance=±5% resistance=22k package=THT]
  Q2 = Basic FET N-Channel [package="TO220 [THT]"]
  R21 = Resistor [tolerance=±5% resistance=100 package=THT]
  R24 = Resistor [tolerance=±5% resistance=1k package=THT]
  R19 = Resistor [tolerance=±5% resistance=470 package=THT]
  R22 = Resistor [tolerance=±5% resistance=100k package=THT]
  C6 = Ceramic Capacitor [capacitance=1µF package="200 mil [THT, multilayer]"]
  S = Pushbutton [package="[THT]"]
  B- = Pushbutton [package="[THT]"]
  B+ = Pushbutton [package="[THT]"]
  Q1 = NPN-Transistor [package="TO92 [THT]"]
  R12 = Resistor [tolerance=±5% resistance=10k package=THT]
  R11 = Resistor [tolerance=±5% resistance=100k package=THT]
  C2 = Ceramic Capacitor [capacitance=1µF package="200 mil [THT, multilayer]"]
  R18 = Resistor [tolerance=±5% resistance=10k package=THT]
  R13 = Resistor [tolerance=±5% resistance=10k package=THT]
  R14 = Resistor [tolerance=±5% resistance=10k package=THT]
  R10 = Resistor [tolerance=±5% resistance=1k package=THT]
  R16 = Resistor [tolerance=±5% resistance=1k package=THT]
  C3 = Ceramic Capacitor [capacitance=100nF package="100 mil [THT, multilayer]"]

nets:
  N1: 7_Seg1.Segment_E, R9.Pin_1
  N2: 7_Seg1.Segment_D, R8.Pin_1
  N3: 7_Seg1.common_cathode, 7_Seg1.Segment_DP
  N4: 7_Seg1.Segment_C, R7.Pin_1
  N5: 7_Seg1.Segment_B, R6.Pin_1
  N6: 7_Seg1.Segment_A, R5.Pin_1
  N7: 7_Seg1.Segment_F, R3.Pin_1
  N8: 7_Seg1.Segment_G, R4.Pin_1
  N9: 4510.In_1, 4510.In_3, 4510.In_4, 4510.In_5, 4510.0V, 4510.Out_5, 4510.Out_4, 4511.In_5, 4511.0V, Clk_G_R_U_O_V_2.pin2, G_I_V_O.pin1, G_I_V_O_2.pin1, G_T_O_V_2.pin1, Q3.E, Q6.E, R28.Pin_1, R17.Pin_1, LED4.cathode, 555.Pin_1, Q4.E, Q5.E, 4060.In_7, 4060.0V, V_O_R_G.pin4, V_O_R_G_2.pin4, LED6.cathode, R18.Pin_1, R13.Pin_1, R14.Pin_1, C3.0
  N10: 4510.In_2, 4511.In_6
  N11: 4510.In_6, 4511.In_7
  N12: 4510.In_7, G_I_V_O.pin2, R29.Pin_0
  N13: 4510.COM_-_Common, Clk_G_R_U_O_V.pin3, Clk_G_R_U_O_V_2.pin3, 4013.1Y, 4060.Out_5, D5.cathode, V_O_R_G.pin3, V_O_R_G_2.pin3, Clk_R.pin2, D3.cathode
  N14: 4510.Out_7, Clk_G_R_U_O_V.pin4, Clk_G_R_U_O_V_2.pin4, R17.Pin_0, U/D_Clk.pin1, D3+.cathode
  N15: 4510.Out_6, 4511.In_1
  N16: 4510.Out_3, 4511.In_2
  N17: 4510.Out_2, Clk_G_R_U_O_V_2.pin1, D6Clk.cathode, D5Clk.cathode, U/D_Clk.pin2, D4-.cathode
  VCC: 4510.Out_1, 4511.In_3, 4511.In_4, 4511.Out_1, Clk_G_R_U_O_V.pin6, G_I_V_O.pin3, R27.Pin_0, R34.Pin_0, J2.pin1, J1.pin1, 4013.VCC, 4081.VCC, V.pin1, V.pin2, GV.pin2, S.Pin_3, S.Pin_4, B-.Pin_3, B-.Pin_4, B+.Pin_3, B+.Pin_4, Q1.C
  N18: 4511.COM_-_Common, R9.Pin_0
  N19: 4511.Out_7, R8.Pin_0
  N20: 4511.Out_6, R7.Pin_0
  N21: 4511.Out_5, R6.Pin_0
  N22: 4511.Out_4, R5.Pin_0
  N23: 4511.Out_3, R4.Pin_0
  N24: 4511.Out_2, R3.Pin_0
  N25: Clk_G_R_U_O_V.pin5, Clk_G_R_U_O_V_2.pin5, G_I_V_O.pin4, G_I_V_O_2.pin4, G_T_O_V.pin2, G_T_O_V_2.pin2, 555.Pin_2
  N26: G_I_V_O_2.pin3, G_T_O_V.pin4, G_T_O_V_2.pin4, 555.Pin_4, 555.Pin_8, R25.Pin_1
  N27: O_V_G.pin1, O_V_G_2.pin1, D3.anode, R23.Pin_0, R20.Pin_0, Q2.source
  N28: O_V_G.pin2, O_V_G_2.pin2, LED1.anode, 4060.Out_1, V_O_R_G.pin1, V_O_R_G_2.pin1, U1.output_voltage, C5.1, GV_3.pin2, GV2.pin2, Q2.drain, R22.Pin_0, C6.0
  GND: O_V_G.pin3, O_V_G_2.pin3, 4013.NC, 4013.1D, 4013.GND, 4013.2A, 4081.GND, G.pin1, G.pin2, D4.anode, +.pin2, GV.pin1, GV_2.pin1, GV_3.pin1, GV2.pin1, R23.Pin_1, R24.Pin_0, R19.Pin_0
  N29: S_B-_B+_DB+.pin1, 4013.1C, S_B-_B+_DB+_2.pin1, S.Pin_2, R18.Pin_0
  N30: S_B-_B+_DB+.pin2, 4081.1A, S_B-_B+_DB+_2.pin2, R16.Pin_1, C3.1
  N31: S_B-_B+_DB+.pin3, 4081.1D, S_B-_B+_DB+_2.pin3, B+.Pin_1, B+.Pin_2, R14.Pin_0, R10.Pin_1
  N32: S_B-_B+_DB+.pin4, 4081.2D, S_B-_B+_DB+_2.pin4, Q1.E, R12.Pin_1
  N33: G_T_O_V.pin3, G_T_O_V_2.pin3, LED2.anode, 555.Pin_3
  N34: Q3.C, R27.Pin_1, C9.0
  N35: Q6.B, C9.1, R28.Pin_0
  N36: Q6.C, R34.Pin_1
  N37: LED1.cathode, R19.Pin_1
  N38: LED2.cathode, R26.Pin_0
  N39: LED4.anode, R31.Pin_0
  N40: 555.Pin_5, R26.Pin_1, C7.1
  N41: 555.Pin_6, 555.Pin_7, R25.Pin_0, C8.0
  N42: C7.0, C8.1
  N43: Q4.B, R32.Pin_0
  N44: Q4.C, J1.pin2
  N45: Q5.B, R33.Pin_0
  N46: Q5.C, J2.pin2
  N47: R31.Pin_1, R32.Pin_1, 4013.1B, 4081.2Y
  N48: R33.Pin_1, D5.anode
  N49: 4013.1A, 4081.1B, 4081.1Y, 4081.2C
  N50: 4081.NC#2, D4-.anode
  N51: 4081.1C, D3+.anode
  N52: 4081.2B, D6Clk.anode
  N53: 4081.NC#10, D5Clk.anode
  N54: 4060.COM_-_Common, C1.1
  N55: 4060.Out_7, R1.Pin_0
  N56: 4060.Out_6, R2.Pin_0
  N57: 4060.Out_2, V_O_R_G.pin2, V_O_R_G_2.pin2, R30.Pin_0, Clk_R.pin1
  N58: C1.0, R1.Pin_1, R2.Pin_1
  N59: R30.Pin_1, LED6.anode
  N60: Fuse2.Connector1, +.pin1
  N61: Fuse2.Connector2, D2.anode
  N62: D2.cathode, D4.cathode, U1.input_voltage, C4.0
  N63: U1.GND, C4.1, C5.0
  N64: R20.Pin_1, Q2.gate, R21.Pin_0
  N65: R21.Pin_1, R24.Pin_1, R22.Pin_1, C6.1
  N66: B-.Pin_2, R13.Pin_0, R16.Pin_0
  N67: Q1.B, R11.Pin_1, C2.1, R10.Pin_0
  N68: R12.Pin_0, R11.Pin_0, C2.0
