# Fritzing sketch schemat_ideowy_pieknego_pcb (saved by Fritzing 0.9.3b)
breadboards: 1

parts:
  7_Seg1 = 7 Segment Display
  4510 = ULN2003A [package="DIP16 [THT]"]
  4511 = ULN2003A [package="DIP16 [THT]"]
  R3 = Resistor [tolerance=±5% resistance=220 package=THT]
  R4 = Resistor [tolerance=±5% resistance=220 package=THT]
  R5 = Resistor [tolerance=±5% resistance=220 package=THT]
  R6 = Resistor [tolerance=±5% resistance=220 package=THT]
  R7 = Resistor [tolerance=±5% resistance=220 package=THT]
  R8 = Resistor [tolerance=±5% resistance=220 package=THT]
  R9 = Resistor [tolerance=±5% resistance=220 package=THT]
  Clk_G_R_U_O_V = female pin header, 6 pins [form="♀ (female)"]
  Clk_G_R_U_O_V_2 = female pin header, 6 pins [form="♀ (female)"]
  G_I_V_O = female pin header, 4 pins [form="♀ (female)"]
  G_I_V_O_2 = female pin header, 4 pins [form="♀ (female)"]
  O_V_G = female pin header, 3 pins [form="♀ (female)"]
  S_B-_B+_DB+ = female pin header, 4 pins [form="♀ (female)"]
  G_T_O_V = female pin header, 4 pins [form="♀ (female)"]
  G_T_O_V_2 = female pin header, 4 pins [form="♀ (female)"]
  Q3 = NPN-Transistor [package="TO92 [THT]"]
  Q6 = NPN-Transistor [package="TO92 [THT]"]
  Q7 = NPN-Transistor [package="TO92 [THT]"]  # not connected
  G_V = female pin header, 2 pins [form="♀ (female)"]
  G_V_2 = female pin header, 2 pins [form="♀ (female)"]
  O_V_G_2 = female pin header, 3 pins [form="♀ (female)"]
  R29 = Resistor [tolerance=±5% resistance=1k package=THT]
  R27 = Resistor [tolerance=±5% resistance=1k package=THT]
  R34 = Resistor [tolerance=±5% resistance=10k package=THT]
  C9 = Ceramic Capacitor [capacitance=100nF package="100 mil [THT, multilayer]"]
  R28 = Resistor [tolerance=±5% resistance=10k package=THT]
  R17 = Resistor [tolerance=±5% resistance=10k package=THT]
  LED1 = LED - 5mm [color="Red (633nm)" package="5 mm [THT]"]  # not connected
  LED2 = LED - 5mm [color="Red (633nm)" package="5 mm [THT]"]
  LED3 = LED - 5mm [color="Red (633nm)" package="5 mm [THT]"]  # not connected
  LED4 = LED - 5mm [color="Red (633nm)" package="5 mm [THT]"]
  LED5 = LED - 5mm [color="Red (633nm)" package="5 mm [THT]"]  # not connected
  555 = 555 Timer [package="DIP8 [THT]"]
  R25 = Resistor [tolerance=±5% resistance=100k package=THT]
  R26 = Resistor [tolerance=±5% resistance=470 package=THT]
  C7 = Ceramic Capacitor [capacitance=100nF package="100 mil [THT, multilayer]"]
  C8 = Ceramic Capacitor [capacitance=100nF package="100 mil [THT, multilayer]"]
  Q4 = NPN-Transistor [package="TO92 [THT]"]
  Q5 = NPN-Transistor [package="TO92 [THT]"]
  R31 = Resistor [tolerance=±5% resistance=470 package=THT]
  R32 = Resistor [tolerance=±5% resistance=1k package=THT]
  J2 = Screw terminal - 2 pins [package=THT]
  J1 = Screw terminal - 2 pins [package=THT]
  R33 = Resistor [tolerance=±5% resistance=1k package=THT]
  4013 = SN74LS20N [package="DIP14 [THT]"]
  4081 = SN74LS20N [package="DIP14 [THT]"]
  4060 = ULN2003A [package="DIP16 [THT]"]
  D5 = Rectifier Diode [part_number=1N4001 package="300 mil [THT]"]
  D6Clk = Rectifier Diode [part_number=1N4001 package="300 mil [THT]"]
  D5Clk = Rectifier Diode [part_number=1N4001 package="300 mil [THT]"]
  U/D_Clk = female pin header, 2 pins [form="♀ (female)"]
  S_B-_B+_DB+_2 = female pin header, 4 pins [form="♀ (female)"]
  V = female pin header, 2 pins [form="♀ (female)"]
  G = female pin header, 2 pins [form="♀ (female)"]
  D3+ = Rectifier Diode [part_number=1N4001 package="300 mil [THT]"]
  D4- = Rectifier Diode [part_number=1N4001 package="300 mil [THT]"]
  V_O_R_G = female pin header, 4 pins [form="♀ (female)"]
  C1 = Ceramic Capacitor [capacitance=100nF package="100 mil [THT, multilayer]"]
  R1 = Resistor [tolerance=±5% resistance=220 package=THT]
  R2 = Resistor [tolerance=±5% resistance=220 package=THT]
  V_O_R_G_2 = female pin header, 4 pins [form="♀ (female)"]
  R30 = Resistor [tolerance=±5% resistance=470 package=THT]
  LED6 = LED - 5mm [color="Red (633nm)" package="5 mm [THT]"]
  Clk_R = female pin header, 2 pins [form="♀ (female)"]

nets:
  N1: 7_Seg1.Segment_E, R9.Pin_1
  N2: 7_Seg1.Segment_D, R8.Pin_1
  N3: 7_Seg1.common_cathode, 7_Seg1.Segment_DP
  N4: 7_Seg1.Segment_C, R7.Pin_1
  N5: 7_Seg1.Segment_B, R6.Pin_1
  N6: 7_Seg1.Segment_A, R5.Pin_1
  N7: 7_Seg1.Segment_F, R3.Pin_1
  N8: 7_Seg1.Segment_G, R4.Pin_1
  N9: 4510.In_1, 4510.In_3, 4510.In_4, 4510.In_5, 4510.0V, 4510.Out_5, 4510.Out_4, 4511.In_5, 4511.0V, Clk_G_R_U_O_V_2.pin2, G_I_V_O.pin1, G_I_V_O_2.pin1, G_T_O_V_2.pin1, Q3.E, Q6.E, R28.Pin_1, R17.Pin_1, LED4.cathode, 555.Ground, Q4.E, Q5.E, 4060.In_7, 4060.0V, V_O_R_G.pin4, V_O_R_G_2.pin4, LED6.cathode
  N10: 4510.In_2, 4511.In_6
  N11: 4510.In_6, 4511.In_7
  N12: 4510.In_7, G_I_V_O.pin2, R29.Pin_0
  N13: 4510.COM_-_Common, Clk_G_R_U_O_V.pin3, Clk_G_R_U_O_V_2.pin3, 4013.1Y, 4060.Out_5, D5.cathode, V_O_R_G_2.pin3, Clk_R.pin2
  N14: 4510.Out_7, Clk_G_R_U_O_V.pin4, Clk_G_R_U_O_V_2.pin4, R17.Pin_0, U/D_Clk.pin1, D3+.cathode
  N15: 4510.Out_6, 4511.In_1
  N16: 4510.Out_3, 4511.In_2
  N17: 4510.Out_2, Clk_G_R_U_O_V_2.pin1, D6Clk.cathode, D5Clk.cathode, U/D_Clk.pin2, D4-.cathode
  N18: 4510.Out_1, 4511.In_3, 4511.In_4, 4511.Out_1, Clk_G_R_U_O_V.pin6, Clk_G_R_U_O_V_2.pin6, G_I_V_O.pin3, R27.Pin_0, R34.Pin_0, J2.pin1, J1.pin1
  N19: 4511.COM_-_Common, R9.Pin_0
  N20: 4511.Out_7, R8.Pin_0
  N21: 4511.Out_6, R7.Pin_0
  N22: 4511.Out_5, R6.Pin_0
  N23: 4511.Out_4, R5.Pin_0
  N24: 4511.Out_3, R4.Pin_0
  N25: 4511.Out_2, R3.Pin_0
  N26: Clk_G_R_U_O_V.pin5, Clk_G_R_U_O_V_2.pin5, G_I_V_O.pin4, G_I_V_O_2.pin4, G_T_O_V.pin2, G_T_O_V_2.pin2, 555.Trigger
  N27: O_V_G.pin1, O_V_G_2.pin1
  N28: O_V_G.pin2, O_V_G_2.pin2
  N29: O_V_G.pin3, O_V_G_2.pin3
  N30: S_B-_B+_DB+.pin1, 4013.1C, S_B-_B+_DB+_2.pin1
  N31: S_B-_B+_DB+.pin2, 4081.1A, S_B-_B+_DB+_2.pin2
  N32: S_B-_B+_DB+.pin3, 4081.1D, S_B-_B+_DB+_2.pin3
  N33: S_B-_B+_DB+.pin4, 4081.2D, S_B-_B+_DB+_2.pin4
  N34: G_T_O_V.pin3, G_T_O_V_2.pin3, LED2.anode, 555.Output
  N35: G_T_O_V.pin4, G_T_O_V_2.pin4, 555.Reset, 555.Vcc_Supply_Voltage, R25.Pin_1
  N36: Q3.C, R27.Pin_1, C9.0
  N37: Q6.B, C9.1, R28.Pin_0
  N38: Q6.C, R34.Pin_1
  N39: G_V.pin1, G_V_2.pin1
  N40: G_V.pin2, G_V_2.pin2
  N41: LED2.cathode, R26.Pin_0
  N42: LED4.anode, R31.Pin_0
  N43: 555.Control_Voltage, R26.Pin_1, C7.1
  N44: 555.Threshold, 555.Discharge, R25.Pin_0, C8.0
  N45: C7.0, C8.1
  N46: Q4.B, R32.Pin_0
  N47: Q4.C, J1.pin2
  N48: Q5.B, R33.Pin_0
  N49: Q5.C, J2.pin2
  N50: R31.Pin_1, R32.Pin_1, 4013.1B, 4081.2Y
  N51: R33.Pin_1, D5.anode
  N52: 4013.1A, 4081.1B, 4081.1Y, 4081.2C
  GND: 4013.NC, 4013.1D, 4013.GND, 4013.2A, 4081.GND, G.pin1, G.pin2
  VCC: 4013.VCC, 4081.VCC, V.pin1, V.pin2
  N53: 4081.NC#2, D4-.anode
  N54: 4081.1C, D3+.anode
  N55: 4081.2B, D6Clk.anode
  N56: 4081.NC#10, D5Clk.anode
  N57: 4060.COM_-_Common, C1.1
  N58: 4060.Out_7, R1.Pin_0
  N59: 4060.Out_6, R2.Pin_0
  N60: 4060.Out_2, V_O_R_G_2.pin2, R30.Pin_0, Clk_R.pin1
  N61: 4060.Out_1, V_O_R_G_2.pin1
  N62: C1.0, R1.Pin_1, R2.Pin_1
  N63: R30.Pin_1, LED6.anode
